// Logisim project ANDGate.circ as structural Verilog: 1 circuit, main circuit main
module main (
  input  in_1,
  input  in_2,
  input  in_3,
  input  in_4,
  input  in_5,
  output out_6
);

  wire and_1_out, or_1_out;

  not not_1 (out_6, in_5);
  and and_1 (and_1_out, in_1, in_2);
  // RGBLED rgbled_1: pin names not known; wires that end beside it: and_1_out
  or or_1 (or_1_out, in_3, in_4);
  // RGBLED rgbled_2: pin names not known; wires that end beside it: or_1_out

  // Notes on the sheet:
  //   AND Gate
  //   NOT Gate
  //   OR Gate
endmodule
