// Logisim project Exercise1-4.circ as structural Verilog: 1 circuit, main circuit main
module main (
  input  in_1,
  input  in_2,
  input  in_3,
  input  A,
  input  B,
  input  A_2,
  input  B_2,
  input  A_3,
  output out_9,
  output AND_Gate,
  output OR_Gate,
  output NOT_Gate
);

  wire and_2_out, and_3_out, and_4_out, not_2_out, not_3_out, not_4_out, not_5_out, not_6_out;

  and and_1 (AND_Gate, A, B);
  or or_1 (OR_Gate, A_2, B_2);
  not not_1 (NOT_Gate, A_3);
  not not_2 (not_2_out, in_3);
  not not_3 (not_3_out, in_1);
  not not_4 (not_4_out, in_3);
  not not_5 (not_5_out, in_1);
  not not_6 (not_6_out, in_2);
  and and_2 (and_2_out, not_2_out, in_2, not_3_out);
  and and_3 (and_3_out, in_1, in_2, not_4_out);
  and and_4 (and_4_out, not_5_out, not_6_out, in_3);
  or or_2 (out_9, and_2_out, and_3_out, and_4_out);

  // Notes on the sheet:
  //   A           B          C
  //   Exercise 1 - 4
endmodule
